# Fritzing sketch IRreperter (saved by Fritzing 0.9.0b)
breadboards: 1

parts:
  Arduino = Arduino Pro Mini v13
  IR_recever = TSOP312.., 314.. [package=THT]
  IR_LED = LTE-302 [package=lte-302]

nets:
  N1: Arduino.VCC, IR_recever.Vs
  GND: Arduino.GND, IR_recever.GND, IR_LED.C
  N2: Arduino.D11_PWM/MOSI, IR_recever.Data
  N3: Arduino.D3_PWM, IR_LED.A
