# Fritzing sketch SerialPortSwitch (saved by Fritzing 0.9.0b)
breadboards: 1

parts:
  Teensy_2_0 = Arduino Pro Mini v13
  TLP521 = TLP621 [package=THT]
  PC_Power_Switch = Round Pushbutton

nets:
  N1: Teensy_2_0.GND, TLP521.Pin_2
  N2: Teensy_2_0.D5_PWM, TLP521.Pin_1
  N3: TLP521.Pin_4, PC_Power_Switch.leg1
  N4: TLP521.Pin_3, PC_Power_Switch.leg0
